// Logisim project ALU.circ as structural Verilog: 9 circuits, main circuit main
module main (
  input  in_1,
  input  in_2,
  input  in_3,
  input  in_4,
  input  in_5,
  input  in_6,
  input  in_7,
  input  in_8,
  input  in_9,
  input  in_10,
  input  in_11,
  input  in_12,
  input  in_13,
  input  in_14,
  input  in_15,
  input  in_16,
  input  in_17,
  input  in_18,
  output out_19,
  output out_20,
  output out_21,
  output out_22,
  output out_23,
  output out_24,
  output out_25,
  output out_26
);
endmodule

// HA
module Half_Adder (
  input  in_1,
  input  in_2,
  output Sum,
  output Carry
);

  wire not_1_out, or_1_out;

  or or_1 (or_1_out, in_1, in_2);
  not not_1 (not_1_out, Carry);
  and and_1 (Carry, in_1, in_2);
  and and_2 (Sum, or_1_out, not_1_out);
endmodule

// FA
module Full_Adder (
  input  in_1,
  input  in_2,
  input  in_3,
  output out_4,
  output out_5
);

  wire half_adder_1_carry, half_adder_1_sum, half_adder_2_carry;

  Half_Adder half_adder_1 (.in_1(in_1), .in_2(in_2), .Sum(half_adder_1_sum), .Carry(half_adder_1_carry));
  Half_Adder half_adder_2 (.in_1(half_adder_1_sum), .in_2(in_3), .Sum(out_4), .Carry(half_adder_2_carry));
  or or_1 (out_5, half_adder_1_carry, half_adder_2_carry);
endmodule

// Add
module _8_Bit_Adder (
  input  [7:0] in_1,
  input  [7:0] in_2,
  output [7:0] out_3,
  output out_4
);

  General_Adder general_adder_1 (.in_1(1'b0), .in_2(in_1), .in_3(in_2), .out_4(out_3), .out_5(out_4));
endmodule

// Sub
module _8_Bit_Subtractor (
  input  [7:0] in_1,
  input  [7:0] in_2,
  output [7:0] out_3
);

  wire [7:0] not_1_out;

  assign not_1_out = ~in_2;  // NOT_Gate not_1, 8 bits wide
  General_Adder general_adder_1 (.in_1(1'b1), .in_2(in_1), .in_3(not_1_out), .out_4(out_3));  // open: out_5
endmodule

// Mult
module _8_by_1_bit_Multiplier (
  input  in_1,
  input  [7:0] in_2,
  output [7:0] out_3
);

  and and_1 (out_3[0], in_2[0], in_1);
  and and_2 (out_3[1], in_2[1], in_1);
  and and_3 (out_3[2], in_2[2], in_1);
  and and_4 (out_3[3], in_2[3], in_1);
  and and_5 (out_3[4], in_2[4], in_1);
  and and_6 (out_3[5], in_2[5], in_1);
  and and_7 (out_3[6], in_2[6], in_1);
  and and_8 (out_3[7], in_2[7], in_1);
endmodule

module _8_Bit_Multiplier (
  input  [7:0] in_1,
  input  [7:0] in_2,
  output [7:0] out_3,
  output out_4
);

  wire [7:0] n8_bit_adder_1_out_3, n8_bit_adder_2_out_3, n8_bit_adder_3_out_3, n8_bit_adder_4_out_3,
       n8_bit_adder_5_out_3, n8_bit_adder_6_out_3, n8_by_1_bit_multiplier_1_out_3,
       n8_by_1_bit_multiplier_2_out_3, n8_by_1_bit_multiplier_3_out_3, n8_by_1_bit_multiplier_4_out_3,
       n8_by_1_bit_multiplier_5_out_3, n8_by_1_bit_multiplier_6_out_3, n8_by_1_bit_multiplier_7_out_3,
       n8_by_1_bit_multiplier_8_out_3, shifter_1_out_2, shifter_2_out_2, shifter_3_out_2, shifter_4_out_2,
       shifter_5_out_2, shifter_6_out_2, shifter_7_out_2, shifter_8_out_2, shifter_9_out_2, shifter_10_out_2,
       shifter_11_out_2, shifter_12_out_2, shifter_13_out_2, shifter_14_out_2, shifter_15_out_2,
       shifter_16_out_2, shifter_17_out_2, shifter_18_out_2, shifter_19_out_2, shifter_20_out_2,
       shifter_21_out_2, shifter_22_out_2, shifter_23_out_2, shifter_24_out_2, shifter_25_out_2,
       shifter_26_out_2, shifter_27_out_2, shifter_28_out_2;

  _8_by_1_bit_Multiplier u_8_by_1_bit_multiplier_1 (
    .in_1(in_2[0]), .in_2(in_1), .out_3(n8_by_1_bit_multiplier_1_out_3));
  _8_by_1_bit_Multiplier u_8_by_1_bit_multiplier_2 (
    .in_1(in_2[1]), .in_2(in_1), .out_3(n8_by_1_bit_multiplier_2_out_3));
  _8_by_1_bit_Multiplier u_8_by_1_bit_multiplier_3 (
    .in_1(in_2[2]), .in_2(in_1), .out_3(n8_by_1_bit_multiplier_3_out_3));
  _8_by_1_bit_Multiplier u_8_by_1_bit_multiplier_4 (
    .in_1(in_2[3]), .in_2(in_1), .out_3(n8_by_1_bit_multiplier_4_out_3));
  _8_by_1_bit_Multiplier u_8_by_1_bit_multiplier_5 (
    .in_1(in_2[4]), .in_2(in_1), .out_3(n8_by_1_bit_multiplier_5_out_3));
  _8_by_1_bit_Multiplier u_8_by_1_bit_multiplier_6 (
    .in_1(in_2[5]), .in_2(in_1), .out_3(n8_by_1_bit_multiplier_6_out_3));
  _8_by_1_bit_Multiplier u_8_by_1_bit_multiplier_7 (
    .in_1(in_2[6]), .in_2(in_1), .out_3(n8_by_1_bit_multiplier_7_out_3));
  _8_by_1_bit_Multiplier u_8_by_1_bit_multiplier_8 (
    .in_1(in_2[7]), .in_2(in_1), .out_3(n8_by_1_bit_multiplier_8_out_3));
  Shifter shifter_1 (.in_1(n8_by_1_bit_multiplier_2_out_3), .out_2(shifter_1_out_2));
  Shifter shifter_2 (.in_1(shifter_3_out_2), .out_2(shifter_2_out_2));
  Shifter shifter_3 (.in_1(n8_by_1_bit_multiplier_3_out_3), .out_2(shifter_3_out_2));
  Shifter shifter_4 (.in_1(shifter_5_out_2), .out_2(shifter_4_out_2));
  Shifter shifter_5 (.in_1(n8_by_1_bit_multiplier_4_out_3), .out_2(shifter_5_out_2));
  Shifter shifter_6 (.in_1(shifter_7_out_2), .out_2(shifter_6_out_2));
  Shifter shifter_7 (.in_1(n8_by_1_bit_multiplier_5_out_3), .out_2(shifter_7_out_2));
  Shifter shifter_8 (.in_1(shifter_9_out_2), .out_2(shifter_8_out_2));
  Shifter shifter_9 (.in_1(n8_by_1_bit_multiplier_6_out_3), .out_2(shifter_9_out_2));
  Shifter shifter_10 (.in_1(n8_by_1_bit_multiplier_7_out_3), .out_2(shifter_10_out_2));
  Shifter shifter_11 (.in_1(shifter_10_out_2), .out_2(shifter_11_out_2));
  Shifter shifter_12 (.in_1(n8_by_1_bit_multiplier_8_out_3), .out_2(shifter_12_out_2));
  Shifter shifter_13 (.in_1(shifter_12_out_2), .out_2(shifter_13_out_2));
  _8_Bit_Adder u_8_bit_adder_1 (
    .in_1(n8_by_1_bit_multiplier_1_out_3), .in_2(shifter_1_out_2), .out_3(n8_bit_adder_1_out_3));  // open: out_4
  Shifter shifter_14 (.in_1(shifter_4_out_2), .out_2(shifter_14_out_2));
  Shifter shifter_15 (.in_1(shifter_6_out_2), .out_2(shifter_15_out_2));
  Shifter shifter_16 (.in_1(shifter_15_out_2), .out_2(shifter_16_out_2));
  Shifter shifter_17 (.in_1(shifter_8_out_2), .out_2(shifter_17_out_2));
  Shifter shifter_18 (.in_1(shifter_17_out_2), .out_2(shifter_18_out_2));
  Shifter shifter_19 (.in_1(shifter_11_out_2), .out_2(shifter_19_out_2));
  Shifter shifter_20 (.in_1(shifter_19_out_2), .out_2(shifter_20_out_2));
  Shifter shifter_21 (.in_1(shifter_13_out_2), .out_2(shifter_21_out_2));
  Shifter shifter_22 (.in_1(shifter_21_out_2), .out_2(shifter_22_out_2));
  _8_Bit_Adder u_8_bit_adder_2 (
    .in_1(n8_bit_adder_1_out_3), .in_2(shifter_2_out_2), .out_3(n8_bit_adder_2_out_3));  // open: out_4
  Shifter shifter_23 (.in_1(shifter_18_out_2), .out_2(shifter_23_out_2));
  Shifter shifter_24 (.in_1(shifter_20_out_2), .out_2(shifter_24_out_2));
  Shifter shifter_25 (.in_1(shifter_22_out_2), .out_2(shifter_25_out_2));
  _8_Bit_Adder u_8_bit_adder_3 (
    .in_1(n8_bit_adder_2_out_3), .in_2(shifter_14_out_2), .out_3(n8_bit_adder_3_out_3));  // open: out_4
  Shifter shifter_26 (.in_1(shifter_24_out_2), .out_2(shifter_26_out_2));
  Shifter shifter_27 (.in_1(shifter_28_out_2), .out_2(shifter_27_out_2));
  Shifter shifter_28 (.in_1(shifter_25_out_2), .out_2(shifter_28_out_2));
  _8_Bit_Adder u_8_bit_adder_4 (
    .in_1(n8_bit_adder_3_out_3), .in_2(shifter_16_out_2), .out_3(n8_bit_adder_4_out_3));  // open: out_4
  _8_Bit_Adder u_8_bit_adder_5 (
    .in_1(n8_bit_adder_4_out_3), .in_2(shifter_23_out_2), .out_3(n8_bit_adder_5_out_3));  // open: out_4
  _8_Bit_Adder u_8_bit_adder_6 (
    .in_1(n8_bit_adder_5_out_3), .in_2(shifter_26_out_2), .out_3(n8_bit_adder_6_out_3));  // open: out_4
  _8_Bit_Adder u_8_bit_adder_7 (.in_1(n8_bit_adder_6_out_3), .in_2(shifter_27_out_2), .out_3(out_3), .out_4(out_4));
endmodule

// GA
module General_Adder (
  input  in_1,
  input  [7:0] in_2,
  input  [7:0] in_3,
  output [7:0] out_4,
  output out_5
);

  wire full_adder_1_out_5, full_adder_2_out_5, full_adder_3_out_5, full_adder_4_out_5, full_adder_5_out_5,
       full_adder_6_out_5, full_adder_7_out_5;

  Full_Adder full_adder_1 (.in_1(in_1), .in_2(in_2[0]), .in_3(in_3[0]), .out_4(out_4[0]), .out_5(full_adder_1_out_5));
  Full_Adder full_adder_2 (
    .in_1(full_adder_1_out_5), .in_2(in_2[1]), .in_3(in_3[1]), .out_4(out_4[1]), .out_5(full_adder_2_out_5));
  Full_Adder full_adder_3 (
    .in_1(full_adder_2_out_5), .in_2(in_2[2]), .in_3(in_3[2]), .out_4(out_4[2]), .out_5(full_adder_3_out_5));
  Full_Adder full_adder_4 (
    .in_1(full_adder_3_out_5), .in_2(in_2[3]), .in_3(in_3[3]), .out_4(out_4[3]), .out_5(full_adder_4_out_5));
  Full_Adder full_adder_5 (
    .in_1(full_adder_4_out_5), .in_2(in_2[4]), .in_3(in_3[4]), .out_4(out_4[4]), .out_5(full_adder_5_out_5));
  Full_Adder full_adder_6 (
    .in_1(full_adder_5_out_5), .in_2(in_2[5]), .in_3(in_3[5]), .out_4(out_4[5]), .out_5(full_adder_6_out_5));
  Full_Adder full_adder_7 (
    .in_1(full_adder_6_out_5), .in_2(in_2[6]), .in_3(in_3[6]), .out_4(out_4[6]), .out_5(full_adder_7_out_5));
  Full_Adder full_adder_8 (.in_1(full_adder_7_out_5), .in_2(in_2[7]), .in_3(in_3[7]), .out_4(out_4[7]), .out_5(out_5));
endmodule

module Shifter (
  input  [7:0] in_1,
  output [7:0] out_2
);


  assign out_2 = {in_1[6:0], 1'b0};
endmodule
