// Logisim project Main.circ as structural Verilog: 2 circuits, main circuit main
module main (
  input  in_1,
  input  in_2,
  output [7:0] out_3
);

  wire [7:0] Address, multiplexer_1_out, n8bit_adder_1_p1;

  Register #(.width(16)) ACC ();  // open: D, en, Q, clk, clr
  RAM ram_1 ();  // open: addr, data, sel, clk, ld, clr
  Multiplexer #(.width(8), .enable("false")) multiplexer_1 (
    .in0(Address), .in1(n8bit_adder_1_p1), .out(multiplexer_1_out), .sel(in_1));
  // _8bit_Adder 8bit_adder_1: pin names not known; wires that end beside it: n8bit_adder_1_p1, out_3, 8'h1
  Program_Counter PC (.in(multiplexer_1_out), .load(in_2), .out(out_3));
  Register #(.width(16)) IR ();  // open: D, en, Q, clk, clr

  // Other names for the same wires on the sheet: pcload = in_2; pcsel = in_1
endmodule

module Program_Counter (
  input  [7:0] in,
  input  load,
  output [7:0] out
);

  wire and_1_out, clock_1_out;

  and and_1 (and_1_out, clock_1_out, load);
  Clock clock_1 (.out(clock_1_out));
  D_Flip_Flop d_ff_1 (.clk(and_1_out), .D(in[0]), .Q(out[0]));  // open: Qn, preset, en, reset
  D_Flip_Flop d_ff_2 (.clk(and_1_out), .D(in[1]), .Q(out[1]));  // open: Qn, preset, en, reset
  D_Flip_Flop d_ff_3 (.clk(and_1_out), .D(in[2]), .Q(out[2]));  // open: Qn, preset, en, reset
  D_Flip_Flop d_ff_4 (.clk(and_1_out), .D(in[3]), .Q(out[3]));  // open: Qn, preset, en, reset
  D_Flip_Flop d_ff_5 (.clk(and_1_out), .D(in[4]), .Q(out[4]));  // open: Qn, preset, en, reset
  D_Flip_Flop d_ff_6 (.clk(and_1_out), .D(in[5]), .Q(out[5]));  // open: Qn, preset, en, reset
  D_Flip_Flop d_ff_7 (.clk(and_1_out), .D(in[6]), .Q(out[6]));  // open: Qn, preset, en, reset
  D_Flip_Flop d_ff_8 (.clk(and_1_out), .D(in[7]), .Q(out[7]));  // open: Qn, preset, en, reset
endmodule
